# Fritzing sketch bbw_1.0 (saved by Fritzing 0.9.3b)

parts:
  Raspberry_Pi_1 = Raspberry Pi 3 [part_number=RPI-3-V1.2]
  LED1 = RGB LED - (4 legs) [package="5 mm [THT]"]
  hc-sr1 = hc-sr04
  R1 = Resistor [tolerance=±5% resistance=1k package="0402 [SMD]"]
  R2 = Resistor [tolerance=±5% resistance=1k package=THT]
  R3 = Resistor [tolerance=±5% resistance=1k package=THT]
  SP1 = SPEAKER [package=pcb_mount_speaker]

nets:
  3V3: Raspberry_Pi_1.3v3, Raspberry_Pi_1.3V3, LED1.common_anode
  N1: Raspberry_Pi_1.GPIO2, LED1.red_cathode
  N2: Raspberry_Pi_1.GPIO3, LED1.green_cathode
  N3: Raspberry_Pi_1.GIPO4, LED1.blue_cathode
  N4: Raspberry_Pi_1.GIPO19, hc-sr1.Trig
  N5: Raspberry_Pi_1.GIPO26, R1.Pin_1
  GND: Raspberry_Pi_1.GND, hc-sr1.GND, R3.Pin_1, SP1.-
  N6: Raspberry_Pi_1.GIPO21, SP1.+
  5V: Raspberry_Pi_1.5V, hc-sr1.VCC
  N7: hc-sr1.Echo, R1.Pin_0, R2.Pin_0
  N8: R2.Pin_1, R3.Pin_0

custom parts:
  hc-sr04: This is a HC-SR04 Distance Sensor
