# Fritzing sketch bbw_1.1 (saved by Fritzing 0.9.3b)

parts:
  Raspberry_Pi_1 = Raspberry Pi 3 [part_number=RPI-3-V1.2]
  LED1 = RGB LED - (4 legs) [package="5 mm [THT]"]
  SP1 = SPEAKER [package=pcb_mount_speaker]
  元件1 = Adafruit VL53L0X Time of Flight Distance Sensor [part_number="Adafruit #3317"]
  R1 = Resistor [tolerance=±5% resistance=330 package=THT]
  R2 = Resistor [tolerance=±5% resistance=330 package=THT]
  R3 = Resistor [tolerance=±5% resistance=330 package=THT]

nets:
  3V3: Raspberry_Pi_1.3v3, Raspberry_Pi_1.3V3, LED1.common_anode
  N1: Raspberry_Pi_1.GPIO2, R1.Pin_1
  N2: Raspberry_Pi_1.GPIO3, R2.Pin_1
  N3: Raspberry_Pi_1.GIPO4, R3.Pin_1
  GND: Raspberry_Pi_1.GND, SP1.-, 元件1.GND
  N4: Raspberry_Pi_1.GIPO21, SP1.+, 元件1.VIN
  N5: Raspberry_Pi_1.GIPO20, 元件1.SDA
  N6: Raspberry_Pi_1.GIPO16, 元件1.SCL
  N7: LED1.red_cathode, R1.Pin_0
  N8: LED1.green_cathode, R2.Pin_0
  N9: LED1.blue_cathode, R3.Pin_0

custom parts:
  Adafruit VL53L0X Time of Flight Distance Sensor: The VL53L0X is a Time of Flight distance sensor like no other you've used! The sensor contains a very tiny invisible laser source, and a matching sensor. The VL53L0X can detect the "time of flight", or how long the light has taken to bounce back to the sensor. Since it uses a very narrow light source, it is good for determining distance of only the surface directly in front of it. Unlike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
